# Fritzing sketch AdfaberArduino2020 (saved by Fritzing 0.9.4)
breadboards: 1

parts:
  R1 = PHOTOCELL [package=photocell]
  OLED1 = OLED 128x64 I2C Monochrome Display
  Part2 = IFR520 MOS module [package=THT]
  S1 = Pushbutton [package="[THT]"]
  M1 = DC Motor
  BAT1 = Battery Holders [package=battery-aa]
  J1 = Piezo Speaker
  S2 = Pushbutton [package="[THT]"]
  S3 = Pushbutton [package="[THT]"]
  WeMos_D1_Mini1 = WeMos D1 Mini
  DHT11_--_Modulul_folosit_are_rezistor = DHT11 Humitidy and Temperature Sensor (3 pins)
  ZS-042_RTC1 = ZS-042 RTC Module
  R2 = Resistor [tolerance=±5% resistance=4.7k package=THT]
  R3 = Resistor [tolerance=±5% resistance=10k package="2512 [SMD]"]
  R4 = Resistor [tolerance=±5% resistance=10k package="2512 [SMD]"]
  R5 = Resistor [tolerance=±5% resistance=10k package="2512 [SMD]"]
  LED1 = LED - 5mm [color="White (4500K)" current=10mA package="5 mm [THT]"]
  R6 = Resistor [tolerance=±5% resistance=220 package="2512 [SMD]"]

nets:
  N1: R1.P$1, WeMos_D1_Mini1.A0, R2.Pin_0
  VDD: R1.P$2, OLED1.VDD, S1.Pin_1, S1.Pin_2, S2.Pin_1, S2.Pin_2, S3.Pin_1, S3.Pin_2, WeMos_D1_Mini1.5V, DHT11_--_Modulul_folosit_are_rezistor.VDD, ZS-042_RTC1.VCC
  GND: OLED1.GND, Part2.pin3, J1.pin1, WeMos_D1_Mini1.G, DHT11_--_Modulul_folosit_are_rezistor.GND, ZS-042_RTC1.GND, R2.Pin_1, R3.Pin_1, R4.Pin_1, R5.Pin_1, LED1.cathode
  N2: OLED1.SCK, WeMos_D1_Mini1.D1, ZS-042_RTC1.SCL
  N3: OLED1.SDA, WeMos_D1_Mini1.D2, ZS-042_RTC1.SDA
  N4: Part2.pin1, WeMos_D1_Mini1.D4
  N5: Part2.pin4, M1.pin_1
  N6: Part2.pin5, M1.pin_2
  N7: Part2.pin6, BAT1.+
  N8: Part2.pin7, BAT1.-
  N9: S1.Pin_3, S1.Pin_4, WeMos_D1_Mini1.D5, R3.Pin_0
  N10: J1.pin2, WeMos_D1_Mini1.D8
  N11: S2.Pin_3, S2.Pin_4, WeMos_D1_Mini1.D6, R4.Pin_0
  N12: S3.Pin_3, S3.Pin_4, WeMos_D1_Mini1.D7, R5.Pin_0
  N13: WeMos_D1_Mini1.D0, R6.Pin_0
  N14: WeMos_D1_Mini1.D3, DHT11_--_Modulul_folosit_are_rezistor.DATA
  N15: LED1.anode, R6.Pin_1

custom parts:
  DHT11 Humitidy and Temperature Sensor (3 pins): DHT11 Humidity and Temperature Sensor (3 pins) from the design created by John De Cristofaro for Adafruit Industries.
